# Fritzing sketch Vdetect (saved by Fritzing 0.9.5d)

parts:
  Part1 = InvenSense MPU6050
  esp1 = ESP32 DevKitc V4
  M1 = NEO-6M GPS Module [part_number=GY-GPS6MV2]
  A7680C = SIM800L BO
  LED1 = LED - 5mm [color="Red (633nm)" package="5 mm [THT]"]
  S1 = Round Pushbutton
  J1 = Piezo Speaker
  R1 = Resistor [tolerance=±5% resistance=220 package="1206 [SMD]"]

nets:
  VCC: Part1.VCC, esp1.3V3
  GND: Part1.GND, esp1.GND, M1.GND, A7680C.pin_6, S1.leg1, J1.pin1, R1.Pin_1
  N1: Part1.SCL, esp1.IO22
  N2: Part1.SDA, esp1.IO21
  N3: esp1.IO4, S1.leg0
  N4: esp1.IO16, M1.Tx
  N5: esp1.IO17, M1.Rx
  N6: esp1.IO18, J1.pin2
  N7: esp1.IO19, LED1.anode
  N8: esp1.IO26, A7680C.pin_5
  N9: esp1.IO27, A7680C.pin_4
  5V: esp1.5V, M1.Vcc, A7680C.PIN2, A7680C.PIN3
  N10: LED1.cathode, R1.Pin_0

custom parts:
  ESP32 DevKitc V4: ESP32-DevKitC board with ESP32-WROOM-32 module. ESP32-DevKitC V4 is a small-sized ESP32-based development board produced by Espressif. Most of the pins on the ESP module are broken out to the pin headers on the board. The pins D0, D1, D2, D3, CMD and CLK are used internally for communication between ESP32 and SPI flash memory. They are grouped on both sides near the USB connector. Avoid using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
  NEO-6M GPS Module: GY-GPS6MV2 NEO-6M GPS Module Module based on U-blox NEO-6M GPS engine, incorporating regulator for 3.3-5V DC input, MS621FE-compatible rechargeable battery for backup and EEPROM for storing configuration settings. Links: NEO-6 series product information page NEO-6 Datasheet
